# Fritzing sketch wire (saved by Fritzing 0.9.10b)
breadboards: 1

parts:
  Part2 = Adafruit BME680 [part_number="Adafruit #3660"]
  S1 = Pushbutton [package="[THT]"]
  S2 = Pushbutton [package="[THT]"]
  Part3 = Adafruit AS7341
  M1 = MAX7219 8x8 single Led Matrix Module
  R1 = Resistor [tolerance=±5% resistance=10k package="2010 [SMD]"]
  R2 = Resistor [tolerance=±5% resistance=10k package="2010 [SMD]"]
  U1 = LIPO-110mAh [package=lipo-110]  # not connected
  Part4 = Arduino Leonardo (Rev3b)

nets:
  N1: Part2.SDI/SDA, Part3.SCL, Part4.SCL
  VCC: Part2.VCC, S1.Pin_3, S1.Pin_4, S2.Pin_3, S2.Pin_4, Part3.VCC, M1.I-CLK-1, M1.O-CLK-1, Part4.5V
  GND: Part2.GND, Part3.GND, M1.I-CS-1, M1.O-CS-1, R1.Pin_1, R2.Pin_1, Part4.GND
  N2: Part2.SCK/SCL, Part3.SDA, Part4.SDA
  N3: S1.Pin_1, S1.Pin_2, R1.Pin_0, Part4.D7
  N4: S2.Pin_1, S2.Pin_2, R2.Pin_0, Part4.D6_PWM/A7
  N5: M1.I-DIN-1, Part4.D11_PWM
  N6: M1.I-GND-1, M1.O-GND-1, Part4.D10_PWM/A10
  N7: M1.I-VCC-1, M1.O-VCC-1, Part4.D13_PWM

custom parts:
  MAX7219 8x8 single Led Matrix Module: Description: MAX7219 8x8 LedMatrix single Red Module Dimensions: 32x32mm Documents:
